// Logisim project q2.circ as structural Verilog: 3 circuits, main circuit main
module main (
  input  [1:0] in,
  input  reset,
  output [1:0] out_3
);

  wire clock_1_out, clock_2_out, counter_1_q;
  wire [2:0] multiplexer_1_out, register_1_q, status_1_s0_;

  Clock clock_1 (.out(clock_1_out));
  Multiplexer #(.width(3), .enable("false")) multiplexer_1 (
    .in0(3'b000), .in1(register_1_q), .out(multiplexer_1_out), .sel(counter_1_q));
  Counter #(.width(1), .max('h1), .ongoal("stay")) counter_1 (
    .Q(counter_1_q), .clk(clock_1_out), .clr(reset));  // open: load, D, count, carry
  status status_1 (
    .s2(multiplexer_1_out[2]), .s1(multiplexer_1_out[1]), .s0(multiplexer_1_out[0]), .i1(in[1]), .i0(in[0]),
    .s2_(status_1_s0_[2]), .s1_(status_1_s0_[1]), .s0_(status_1_s0_[0]));
  Clock clock_2 (.out(clock_2_out));
  Register #(.width(3)) register_1 (.D(status_1_s0_), .Q(register_1_q), .clk(clock_2_out), .clr(reset));  // open: en
  \output  output_1 (
    .s2(register_1_q[2]), .s1(register_1_q[1]), .s0(register_1_q[0]), .i1(in[1]), .i0(in[0]),
    .out1(out_3[1]), .out0(out_3[0]));
endmodule

module status (
  input  s2,
  input  s1,
  input  s0,
  input  i1,
  input  i0,
  output s2_,
  output s1_,
  output s0_
);

  wire and_1_out, and_2_out, and_3_out, and_4_out, and_5_out, and_6_out, not_1_out, not_2_out, not_3_out,
       not_4_out, not_5_out, not_6_out, not_7_out, not_8_out, not_9_out, not_10_out;

  not not_1 (not_1_out, s2);
  not not_2 (not_2_out, s1);
  not not_3 (not_3_out, s0);
  not not_4 (not_4_out, s2);
  not not_5 (not_5_out, i1);
  not not_6 (not_6_out, i0);
  not not_7 (not_7_out, s2);
  not not_8 (not_8_out, s0);
  not not_9 (not_9_out, s1);
  not not_10 (not_10_out, s0);
  and and_1 (and_1_out, s1, s0, i0);
  and and_2 (and_2_out, not_1_out, s1, i0);
  and and_3 (and_3_out, s2, not_2_out, not_3_out, i0);
  and and_4 (and_4_out, not_4_out, s0, not_5_out, not_6_out);
  and and_5 (and_5_out, not_7_out, s1, not_8_out, i1);
  and and_6 (and_6_out, s2, not_9_out, not_10_out, i0);
  or or_1 (s0_, i1, and_1_out);
  or or_2 (s2_, and_2_out, and_3_out);
  or or_3 (s1_, and_4_out, and_5_out, and_6_out);
endmodule

module \output  (
  input  s2,
  input  s1,
  input  s0,
  input  i1,
  input  i0,
  output out1,
  output out0
);

  wire not_1_out, not_2_out, not_3_out, not_4_out, not_5_out;

  not not_1 (not_1_out, s2);
  not not_2 (not_2_out, i1);
  not not_3 (not_3_out, s1);
  not not_4 (not_4_out, s0);
  not not_5 (not_5_out, i1);
  and and_1 (out1, not_1_out, s1, s0, not_2_out, i0);
  and and_2 (out0, s2, not_3_out, not_4_out, not_5_out, i0);
endmodule
