// Logisim project P0_Q1_L0_CRC.circ as structural Verilog: 3 circuits, main circuit CRC
module CRC (
  input  [7:0] A,
  input  [3:0] B,
  output [10:0] O
);

  wire [2:0] \四位模二除法器_1_余数 , \四位模二除法器_2_余数 , \四位模二除法器_3_余数 , \四位模二除法器_4_余数 , \四位模二除法器_5_余数 , \四位模二除法器_6_余数 ;
  wire [3:1] \四位模二除法器_7_余数 ;

  \四位模二除法器  \u_四位模二除法器_1  (.\被除数 (A[7:4]), .\除数 (B), .\余数 (\四位模二除法器_1_余数 ));  // open: out_3
  \四位模二除法器  \u_四位模二除法器_2  (.\被除数 ({\四位模二除法器_1_余数 , A[3]}), .\除数 (B), .\余数 (\四位模二除法器_2_余数 ));  // open: out_3
  \四位模二除法器  \u_四位模二除法器_3  (.\被除数 ({\四位模二除法器_2_余数 , A[2]}), .\除数 (B), .\余数 (\四位模二除法器_3_余数 ));  // open: out_3
  \四位模二除法器  \u_四位模二除法器_4  (.\被除数 ({\四位模二除法器_3_余数 , A[1]}), .\除数 (B), .\余数 (\四位模二除法器_4_余数 ));  // open: out_3
  \四位模二除法器  \u_四位模二除法器_5  (.\被除数 ({\四位模二除法器_4_余数 , A[0]}), .\除数 (B), .\余数 (\四位模二除法器_5_余数 ));  // open: out_3
  \四位模二除法器  \u_四位模二除法器_6  (.\被除数 ({\四位模二除法器_5_余数 , 1'b0}), .\除数 (B), .\余数 (\四位模二除法器_6_余数 ));  // open: out_3
  \四位模二除法器  \u_四位模二除法器_7  (.\被除数 ({\四位模二除法器_6_余数 , 1'b0}), .\除数 (B), .\余数 (\四位模二除法器_7_余数 ));  // open: out_3
  \四位模二除法器  \u_四位模二除法器_8  (.\被除数 ({\四位模二除法器_7_余数 , 1'b0}), .\除数 (B), .\余数 (O[2:0]));  // open: out_3

  assign O[10:3] = A;

  // Other names for the same wires on the sheet: 被除数[7:0] = A; 校验码[2:0] = O[2:0]; 除数[3:0] = B
endmodule

module \四位模二除法器  (
  input  [3:0] \被除数 ,
  input  [3:0] \除数 ,
  output out_3,
  output [2:0] \余数 
);

  wire [1:0] bitfinder_1_index;
  wire [3:0] _0ordivision, shifter_1_out, xor_1_out;

  assign xor_1_out = \被除数  ^ _0ordivision;  // XOR_Gate xor_1, 4 bits wide
  Bit_Extender #(.in_width(4), .out_width(3)) bit_extender_1 (.in(xor_1_out), .out(\余数 ));
  \generate  generate_1 (
    .a0(\除数 [0]), .a1(\除数 [1]), .a2(\除数 [2]), .a3(\除数 [3]), .div(out_3), .b0(_0ordivision[0]),
    .b1(_0ordivision[1]), .b2(_0ordivision[2]), .b3(_0ordivision[3]));
  BitFinder #(.width(4), .\type ("high1")) bitfinder_1 (.in(\被除数 ), .index(bitfinder_1_index));  // open: found
  Shifter #(.width(4)) shifter_1 (.in(4'b0001), .\dist (bitfinder_1_index), .out(shifter_1_out));
  Comparator #(.width(4), .mode("unsigned")) comparator_1 (.a(shifter_1_out), .b(4'b1000), .eq(out_3));  // open: gt, lt

  // Other names for the same wires on the sheet: 商 = out_3
endmodule

module \generate  (
  input  a0,
  input  a1,
  input  a2,
  input  a3,
  input  div,
  output b0,
  output b1,
  output b2,
  output b3
);

  and and_1 (b0, a0, div);
  and and_2 (b1, a1, div);
  and and_3 (b2, a2, div);

  assign b3 = div;
endmodule
