// Logisim project P0_Q3_L1_navigation_2020.circ as structural Verilog: 3 circuits, main circuit navigation
module navigation (
  input  [1:0] dir,
  input  clk,
  input  reset,
  output arrive,
  output hit
);

  wire hit_t, \赋初值_q ;
  wire [2:0] multiplexer_1_out, status_mem_q, \状态_1_status_ne ;

  Counter #(.width(1), .max('h1), .ongoal("stay")) \u_赋初值  (
    .Q(\赋初值_q ), .clk(clk), .clr(reset));  // open: load, D, count, carry
  Multiplexer #(.width(3)) multiplexer_1 (
    .in0(3'b000), .in1(status_mem_q), .out(multiplexer_1_out), .sel(\赋初值_q ));  // open: en
  \状态  \u_状态_1  (.status(multiplexer_1_out), .dir(dir), .status_ne(\状态_1_status_ne ), .hit(hit_t));
  Register #(.width(1)) register_1 (.D(hit_t), .Q(hit), .clk(clk), .clr(reset));  // open: en
  Register #(.width(3)) status_mem (.D(\状态_1_status_ne ), .Q(status_mem_q), .clk(clk), .clr(reset));  // open: en
  \输出  \u_输出_1  (.status_ne(status_mem_q), .arrive(arrive));
endmodule

module \状态  (
  input  [2:0] status,
  input  [1:0] dir,
  output [2:0] status_ne,
  output hit
);

  wire and_1_out, and_2_out, and_3_out, and_4_out, and_5_out, and_6_out, and_7_out, and_8_out, and_9_out,
       and_10_out, and_11_out, and_12_out, and_13_out, and_14_out, and_15_out, and_16_out, and_17_out,
       not_1_out, not_2_out, not_3_out, not_4_out, not_5_out, not_6_out, not_7_out, not_8_out, not_9_out,
       not_10_out, not_11_out, not_12_out, not_13_out, not_14_out, not_15_out, not_16_out, not_17_out,
       not_18_out, not_19_out, not_20_out, not_21_out, not_22_out, not_23_out, not_24_out, not_25_out,
       not_26_out, not_27_out, not_28_out, not_29_out, not_30_out, not_31_out, not_32_out, not_33_out;

  not not_1 (not_1_out, status[0]);
  not not_2 (not_2_out, dir[1]);
  not not_3 (not_3_out, dir[1]);
  not not_4 (not_4_out, dir[0]);
  not not_5 (not_5_out, status[0]);
  not not_6 (not_6_out, dir[1]);
  not not_7 (not_7_out, dir[0]);
  not not_8 (not_8_out, status[0]);
  not not_9 (not_9_out, dir[0]);
  not not_10 (not_10_out, status[2]);
  not not_11 (not_11_out, status[1]);
  not not_12 (not_12_out, status[0]);
  not not_13 (not_13_out, dir[1]);
  not not_14 (not_14_out, dir[0]);
  not not_15 (not_15_out, status[2]);
  not not_16 (not_16_out, status[1]);
  not not_17 (not_17_out, status[0]);
  not not_18 (not_18_out, status[2]);
  not not_19 (not_19_out, status[1]);
  not not_20 (not_20_out, status[0]);
  not not_21 (not_21_out, status[2]);
  not not_22 (not_22_out, status[1]);
  not not_23 (not_23_out, status[2]);
  not not_24 (not_24_out, status[0]);
  not not_25 (not_25_out, status[0]);
  not not_26 (not_26_out, dir[1]);
  not not_27 (not_27_out, dir[0]);
  not not_28 (not_28_out, dir[1]);
  not not_29 (not_29_out, dir[0]);
  and and_1 (and_1_out, status[1], not_1_out, not_2_out, dir[0]);
  and and_2 (and_2_out, status[1], status[0], not_3_out, not_4_out);
  not not_30 (not_30_out, status[1]);
  and and_3 (and_3_out, not_30_out, status[0], not_31_out);
  not not_31 (not_31_out, dir[1]);
  and and_4 (and_4_out, status[0], not_32_out, dir[0]);
  not not_32 (not_32_out, dir[1]);
  and and_5 (and_5_out, status[1], not_5_out, not_6_out, not_7_out);
  and and_6 (and_6_out, status[1], not_8_out, dir[1], dir[0]);
  and and_7 (and_7_out, status[1], status[0], dir[1], not_9_out);
  and and_8 (and_8_out, not_10_out, not_11_out, not_12_out, not_13_out, not_14_out);
  and and_9 (and_9_out, status[0], dir[0]);
  and and_10 (and_10_out, status[1], dir[1], not_33_out);
  not not_33 (not_33_out, dir[0]);
  and and_11 (and_11_out, not_15_out, not_16_out, not_17_out, dir[0]);
  and and_12 (and_12_out, not_18_out, not_19_out, not_20_out, dir[1]);
  and and_13 (and_13_out, not_21_out, not_22_out, dir[1], dir[0]);
  and and_14 (and_14_out, not_23_out, not_24_out, dir[1], dir[0]);
  and and_15 (and_15_out, status[1], not_25_out, not_26_out, not_27_out);
  and and_16 (and_16_out, status[1], status[0], not_28_out, dir[0]);
  and and_17 (and_17_out, status[1], status[0], dir[1], not_29_out);
  or or_1 (status_ne[2], and_1_out, and_2_out);
  or or_2 (status_ne[1], and_3_out, and_4_out, and_5_out, and_6_out, and_7_out);
  or or_3 (status_ne[0], and_8_out, and_9_out, and_10_out);
  or or_4 (hit, and_11_out, and_12_out, and_13_out, and_14_out, and_15_out, and_16_out, and_17_out);
endmodule

module \输出  (
  input  [2:0] status_ne,
  output arrive
);


  assign arrive = status_ne[2];
endmodule
