// Logisim project P0_Q4_L0_FSM.circ as structural Verilog: 4 circuits, main circuit fsm
module fsm (
  input  CLR,
  input  [1:0] In,
  output out_3
);

  wire clk;
  wire [3:0] multiplexer_1_out, state, \状态_1_s0_ ;

  Clock clock_1 (.out(clk));
  // Probe on state
  \状态  \u_状态_1  (
    .s3(state[3]), .s2(state[2]), .s1(state[1]), .s0(state[0]), .in1(In[1]), .in0(In[0]),
    .s3_(\状态_1_s0_ [3]), .s2_(\状态_1_s0_ [2]), .s1_(\状态_1_s0_ [1]), .s0_(\状态_1_s0_ [0]));
  \输出  \u_输出_1  (.s3(state[3]), .s2(state[2]), .s1(state[1]), .s0(state[0]), .in1(In[1]), .in0(In[0]), .z(out_3));
  // Probe on \状态_1_s0_ 
  Multiplexer #(.width(4), .enable("false")) multiplexer_1 (
    .in0(\状态_1_s0_ ), .in1(4'b0000), .out(multiplexer_1_out), .sel(CLR));
  // Probe on state
  Register #(.width(4)) register_1 (.D(multiplexer_1_out), .Q(state), .clk(clk));  // open: en, clr

  // Other names for the same wires on the sheet: Z = out_3
endmodule

module \状态  (
  input  s3,
  input  s2,
  input  s1,
  input  s0,
  input  in1,
  input  in0,
  output s3_,
  output s2_,
  output s1_,
  output s0_
);

  wire and_1_out, and_2_out, and_3_out, and_4_out, and_5_out, and_6_out, and_7_out, and_8_out, and_9_out,
       and_10_out, and_11_out, and_12_out, and_13_out, and_14_out, and_15_out, and_16_out, and_17_out,
       and_18_out, and_19_out, and_20_out, and_21_out, and_22_out, not_1_out, not_2_out, not_3_out,
       not_4_out, not_5_out, not_6_out, not_7_out, not_8_out, not_9_out, not_10_out, not_11_out, not_12_out,
       not_13_out, not_14_out, not_15_out, not_16_out, not_17_out, not_18_out, not_19_out, not_20_out,
       not_21_out, not_22_out, not_23_out, not_24_out, not_25_out, not_26_out, not_27_out, not_28_out,
       not_29_out, not_30_out, not_31_out, not_32_out, not_33_out, not_34_out, not_35_out, not_36_out,
       not_37_out, not_38_out, not_39_out, not_40_out, not_41_out, not_42_out, not_43_out, not_44_out,
       not_45_out, not_46_out, not_47_out, not_48_out, not_49_out, not_50_out, not_51_out, not_52_out,
       not_53_out, not_54_out, not_55_out, not_56_out, not_57_out, not_58_out, not_59_out, not_60_out,
       not_61_out, not_62_out, not_63_out, not_64_out, not_65_out, not_66_out, not_67_out;

  not not_1 (not_1_out, s3);
  not not_2 (not_2_out, s2);
  not not_3 (not_3_out, in0);
  not not_4 (not_4_out, s3);
  not not_5 (not_5_out, s1);
  not not_6 (not_6_out, s0);
  not not_7 (not_7_out, in0);
  not not_8 (not_8_out, s2);
  not not_9 (not_9_out, s1);
  not not_10 (not_10_out, in0);
  not not_11 (not_11_out, s2);
  not not_12 (not_12_out, s0);
  not not_13 (not_13_out, in0);
  not not_14 (not_14_out, s3);
  not not_15 (not_15_out, s2);
  not not_16 (not_16_out, s1);
  not not_17 (not_17_out, in1);
  not not_18 (not_18_out, s3);
  not not_19 (not_19_out, s2);
  not not_20 (not_20_out, in1);
  not not_21 (not_21_out, in0);
  not not_22 (not_22_out, s2);
  not not_23 (not_23_out, s0);
  not not_24 (not_24_out, in0);
  not not_25 (not_25_out, s2);
  not not_26 (not_26_out, s1);
  not not_27 (not_27_out, in0);
  not not_28 (not_28_out, s3);
  not not_29 (not_29_out, s2);
  not not_30 (not_30_out, s1);
  not not_31 (not_31_out, in0);
  not not_32 (not_32_out, s3);
  not not_33 (not_33_out, s2);
  not not_34 (not_34_out, in1);
  not not_35 (not_35_out, in0);
  not not_36 (not_36_out, s2);
  not not_37 (not_37_out, s1);
  not not_38 (not_38_out, in1);
  not not_39 (not_39_out, in0);
  not not_40 (not_40_out, s2);
  not not_41 (not_41_out, s0);
  not not_42 (not_42_out, in0);
  not not_43 (not_43_out, s3);
  not not_44 (not_44_out, s1);
  not not_45 (not_45_out, s0);
  not not_46 (not_46_out, in0);
  not not_47 (not_47_out, s0);
  not not_48 (not_48_out, in1);
  not not_49 (not_49_out, s3);
  not not_50 (not_50_out, s2);
  not not_51 (not_51_out, s1);
  not not_52 (not_52_out, in0);
  not not_53 (not_53_out, s3);
  not not_54 (not_54_out, s2);
  not not_55 (not_55_out, in1);
  not not_56 (not_56_out, s2);
  not not_57 (not_57_out, s0);
  not not_58 (not_58_out, in1);
  not not_59 (not_59_out, s3);
  not not_60 (not_60_out, s1);
  not not_61 (not_61_out, s0);
  not not_62 (not_62_out, in1);
  not not_63 (not_63_out, in1);
  not not_64 (not_64_out, in1);
  not not_65 (not_65_out, s2);
  not not_66 (not_66_out, s1);
  not not_67 (not_67_out, in1);
  and and_1 (and_1_out, not_1_out, not_2_out, s1, s0, in1, not_3_out);
  and and_2 (and_2_out, not_4_out, s2, not_5_out, not_6_out, not_7_out);
  and and_3 (and_3_out, s3, not_8_out, not_9_out, s0, not_10_out);
  and and_4 (and_4_out, s3, not_11_out, s1, not_12_out, not_13_out);
  and and_5 (and_5_out, not_14_out, not_15_out, not_16_out, s0, not_17_out, in0);
  and and_6 (and_6_out, not_18_out, not_19_out, s1, not_20_out, not_21_out);
  and and_7 (and_7_out, not_22_out, s1, not_23_out, not_24_out);
  and and_8 (and_8_out, s3, not_25_out, not_26_out, s0, in1, not_27_out);
  and and_9 (and_9_out, not_28_out, not_29_out, not_30_out, s0, not_31_out);
  and and_10 (and_10_out, not_32_out, not_33_out, s0, not_34_out, not_35_out);
  and and_11 (and_11_out, not_36_out, not_37_out, s0, not_38_out, not_39_out);
  and and_12 (and_12_out, not_40_out, s1, not_41_out, in1, not_42_out);
  and and_13 (and_13_out, not_43_out, s2, not_44_out, not_45_out, in1, not_46_out);
  and and_14 (and_14_out, s3, s2, s1, s0, in1, in0);
  and and_15 (and_15_out, not_47_out, not_48_out, in0);
  and and_16 (and_16_out, not_49_out, not_50_out, not_51_out, s0, in1, not_52_out);
  and and_17 (and_17_out, not_53_out, not_54_out, s1, not_55_out);
  and and_18 (and_18_out, not_56_out, s1, not_57_out, not_58_out);
  and and_19 (and_19_out, not_59_out, s2, not_60_out, not_61_out, not_62_out);
  and and_20 (and_20_out, s2, not_63_out, in0);
  and and_21 (and_21_out, s3, not_64_out, in0);
  and and_22 (and_22_out, s3, not_65_out, not_66_out, s0, not_67_out);
  or or_1 (s3_, and_1_out, and_2_out, and_3_out, and_4_out);
  or or_2 (s2_, and_5_out, and_6_out, and_7_out, and_8_out);
  or or_3 (s1_, and_9_out, and_10_out, and_11_out, and_12_out, and_13_out, and_14_out);
  or or_4 (s0_, and_15_out, and_16_out, and_17_out, and_18_out, and_19_out, and_20_out, and_21_out, and_22_out);
endmodule

module \输出  (
  input  s3,
  input  s2,
  input  s1,
  input  s0,
  input  in1,
  input  in0,
  output z
);

  wire and_1_out, and_2_out, and_3_out, and_4_out, not_1_out, not_2_out, not_3_out, not_4_out, not_5_out,
       not_6_out, not_7_out, not_8_out, not_9_out;

  not not_1 (not_1_out, s3);
  not not_2 (not_2_out, s2);
  not not_3 (not_3_out, in0);
  not not_4 (not_4_out, s2);
  not not_5 (not_5_out, s0);
  not not_6 (not_6_out, in0);
  not not_7 (not_7_out, s2);
  not not_8 (not_8_out, s1);
  not not_9 (not_9_out, in0);
  and and_1 (and_1_out, not_1_out, not_2_out, s1, not_3_out);
  and and_2 (and_2_out, not_4_out, s1, not_5_out, not_6_out);
  and and_3 (and_3_out, s3, not_7_out, not_8_out, s0, not_9_out);
  and and_4 (and_4_out, s3, s2, s1, s0);
  or or_1 (z, and_1_out, and_2_out, and_3_out, and_4_out);
endmodule

module \同步复位  (
  input  in,
  input  in_2,
  output out
);

  wire clock_1_out, multiplexer_1_out;

  Multiplexer multiplexer_1 (.in0(in), .in1(1'b0), .out(multiplexer_1_out), .sel(in_2));  // open: en
  Clock clock_1 (.out(clock_1_out));
  Register #(.width(1)) register_1 (.D(multiplexer_1_out), .Q(out), .clk(clock_1_out));  // open: en, clr
endmodule
