// Logisim project P0_Q5_ftoi.circ as structural Verilog: 1 circuit, main circuit ftoi
module ftoi (
  input  [15:0] float,
  output [31:0] \int 
);

  wire comparator_1_gt, comparator_2_lt, comparator_3_eq, comparator_4_eq, nand_1_out, nand_2_out, output3;
  wire [4:0] bit_extender_2_out, or_1_out, shifter_1_out, subtractor_1_out;
  wire [31:0] and_1_out, input_shift, output1, output2, output4, output5, output6, shifter_2_out;

  Comparator #(.width(5), .mode("unsigned")) comparator_1 (
    .a(float[14:10]), .b(5'b01111), .gt(comparator_1_gt));  // open: eq, lt
  Comparator #(.width(5), .mode("unsigned")) comparator_2 (
    .a(float[14:10]), .b(5'b01111), .lt(comparator_2_lt));  // open: gt, eq
  Comparator #(.width(5), .mode("unsigned")) comparator_3 (
    .a(float[14:10]), .b({5{1'b1}}), .eq(comparator_3_eq));  // open: gt, lt
  assign input_shift = {{21{1'b0}}, {1'b1, float[9:0]}};  // Bit_Extender bit_extender_1
  nand nand_1 (nand_1_out, comparator_3_eq, 1'b1);
  nand nand_2 (nand_2_out, comparator_2_lt, 1'b1);
  assign bit_extender_2_out = {{4{1'b0}}, comparator_1_gt};  // Bit_Extender bit_extender_2
  Comparator #(.width(1), .mode("unsigned")) comparator_4 (
    .a(float[15]), .b(1'b1), .eq(comparator_4_eq));  // open: gt, lt
  assign output1 = {{31{1'b0}}, nand_1_out};  // Bit_Extender bit_extender_3
  assign output2 = {{31{1'b0}}, nand_2_out};  // Bit_Extender bit_extender_4
  // Probe on shifter_1_out
  Shifter #(.width(5)) shifter_1 (.in(bit_extender_2_out), .\dist (3'b100), .out(shifter_1_out));
  // Probe on float[14:10]
  Multiplexer #(.width(32)) multiplexer_1 (
    .in0(output4), .in1(output5), .out(output6), .sel(comparator_4_eq));  // open: en
  // Probe on or_1_out
  assign or_1_out = shifter_1_out | float[14:10];  // OR_Gate or_1, 5 bits wide
  // Probe on subtractor_1_out
  Subtractor #(.width(5)) subtractor_1 (.a(or_1_out), .b(5'b01111), .out(subtractor_1_out));  // open: bin, bout
  assign and_1_out = output1 & output2;  // AND_Gate and_1, 32 bits wide
  Shifter #(.width(32)) shifter_2 (.in(input_shift), .\dist (subtractor_1_out), .out(shifter_2_out));
  Multiplexer #(.width(32)) multiplexer_2 (.in0({32{1'b0}}), .in1(output6), .out(\int ), .sel(output3));  // open: en
  Bit_Extender #(.in_width(32), .out_width(1)) bit_extender_5 (.in(and_1_out), .out(output3));
  // Probe on shifter_2_out
  Shifter #(.width(32), .shift("lr")) shifter_3 (.in(shifter_2_out), .\dist (5'b01010), .out(output4));
  Negator #(.width(32)) negator_1 (.in(output4), .out(output5));

  // Other names for the same wires on the sheet: M[4:0] = float[14:10]; 符号 = float[15]
endmodule
