// Logisim project P3_lwor.circ as structural Verilog: 8 circuits, main circuit main
module main (
  input  reset,
  output [31:0] out_2,
  output out_3,
  output [4:0] out_4,
  output [31:0] out_5,
  output out_6,
  output [4:0] out_7,
  output [31:0] out_8
);

  wire ALUsrc, Branch, clk, jalsave, jr, lwor, MemtoReg, PCj, PCSrc, RegDst, sign, Zero;
  wire [2:0] ALUControl;
  wire [4:0] A3_prime, multiplier_1_cout, multiplier_1_out;
  wire [27:0] PC;
  wire [31:0] adder_2_out, adder_3_out, ALUResult, ALUResult1, bit_extender_1_out, lwor_addr,
       multiplexer_1_out, multiplexer_2_out, multiplexer_3_out, multiplexer_6_out, PC_4, PCBranch, ReadData,
       ScrA, shifter_1_out, SignImm, WD3_prime;
  wire [31:28] jumpPC;

  Clock clock_1 (.out(clk));
  Multiplexer #(.width(32), .enable("false")) multiplexer_1 (
    .in0(PC_4), .in1(PCBranch), .out(multiplexer_1_out), .sel(PCSrc));
  Multiplexer #(.width(32), .enable("false")) multiplexer_2 (
    .in0(multiplexer_1_out), .in1({jumpPC, out_2[25:0], 2'b00}), .out(multiplexer_2_out), .sel(PCj));
  Multiplexer #(.width(32), .enable("false")) multiplexer_3 (
    .in0(multiplexer_2_out), .in1(ScrA), .out(multiplexer_3_out), .sel(jr));
  IFU ifu_1 (.clk(clk), .reset(reset), .PC_in(multiplexer_3_out), .Instr(out_2), .PC_4(PC_4), .PC({jumpPC, PC}));
  GRF GRF (
    .A1(out_2[25:21]), .A2(out_2[20:16]), .A3(out_4), .WD(out_5), .reset(reset), .RegWrite(out_3), .clk(clk),
    .RD1(ScrA), .RD2(out_8));
  Multiplexer #(.width(5), .enable("false")) multiplexer_4 (
    .in0(out_2[20:16]), .in1(out_2[15:11]), .out(A3_prime), .sel(RegDst));
  Multiplexer #(.width(5), .enable("false")) multiplexer_5 (
    .in0(A3_prime), .in1({5{1'b1}}), .out(out_4), .sel(jalsave));
  Controller Ctrl (
    .op(out_2[31:26]), .func(out_2[5:0]), .sign(sign), .Branch(Branch), .MemWrite(out_6), .RegWrite(out_3),
    .MemtoReg(MemtoReg), .ALUsrc(ALUsrc), .RegDst(RegDst), .ALUControl(ALUControl), .PCj(PCj),
    .jalsave(jalsave), .jr(jr), .lwor(lwor));
  EXT EXT (.imm(out_2[15:0]), .sign(sign), .SignImm(SignImm));
  Multiplexer #(.width(32), .enable("false")) multiplexer_6 (
    .in0(out_8), .in1(SignImm), .out(multiplexer_6_out), .sel(ALUsrc));
  and and_1 (PCSrc, Branch, Zero);
  ALU ALU (.inA(ScrA), .inB(multiplexer_6_out), .op(ALUControl), .Zero(Zero), .ALUResult(ALUResult1));
  Shifter #(.width(32)) shifter_1 (.in(SignImm), .\dist (5'b00010), .out(shifter_1_out));
  Multiplexer #(.width(32), .enable("false")) multiplexer_7 (
    .in0(ALUResult1), .in1(lwor_addr), .out({ALUResult[31:7], out_7, ALUResult[1:0]}), .sel(lwor));
  Adder #(.width(32)) adder_1 (.a(shifter_1_out), .b(PC_4), .out(PCBranch));  // open: cin, cout
  DM DM (
    .ALUResult({ALUResult[31:7], out_7, ALUResult[1:0]}), .WD(out_8), .clk(clk), .reset(reset), .WE(out_6),
    .RD(ReadData));
  Multiplier #(.width(5)) multiplier_1 (
    .a(out_2[20:16]), .b(5'b00100), .out(multiplier_1_out), .cout(multiplier_1_cout));  // open: cin
  Adder #(.width(32)) adder_2 (.a(ScrA), .b(SignImm), .out(adder_2_out));  // open: cin, cout
  assign bit_extender_1_out = {{22{multiplier_1_cout[4]}}, {multiplier_1_cout, multiplier_1_out}};  // Bit_Extender bit_extender_1
  Multiplexer #(.width(32), .enable("false")) multiplexer_8 (
    .in0({ALUResult[31:7], out_7, ALUResult[1:0]}), .in1(ReadData), .out(WD3_prime), .sel(MemtoReg));
  Adder #(.width(32)) adder_3 (.a(adder_2_out), .b(bit_extender_1_out), .out(adder_3_out));  // open: cin, cout
  assign lwor_addr = 32'h7c & adder_3_out;  // AND_Gate and_2, 32 bits wide
  Multiplexer #(.width(32), .enable("false")) multiplexer_9 (.in0(WD3_prime), .in1(PC_4), .out(out_5), .sel(jalsave));

  // Other names for the same wires on the sheet: A3[4:0] = out_4; ALUResult[6:2] = out_7; Instr[31:0] = out_2;
  //   opt[5:0] = out_2[31:26]; func[5:0] = out_2[5:0]; imm[15:0] = out_2[15:0]; instr_index[25:0] = out_2[25:0];
  //   jumpPC[27:2] = out_2[25:0]; shamt[4:0] = out_2[10:6]; rd[4:0] = out_2[15:11]; rt[4:0] = out_2[20:16];
  //   rs[4:0] = out_2[25:21]; PC[31:28] = jumpPC; MemWrite = out_6; RD2[31:0] = out_8; RegWrite = out_3;
  //   WD3[31:0] = out_5

  // Notes on the sheet:
  //   IFU
  //   GRF中A3的确定
  //   输出
  //   j型指令PC的跳转生成
  //   符号扩展 和 PCBranch
  //   ALU
  //   beq的跳转信号
  //   DM
  //   lwor addr generate
  //   WD3的生成
endmodule

module GRF (
  input  reset,
  input  RegWrite,
  input  clk,
  input  [4:0] A1,
  input  [4:0] A2,
  input  [4:0] A3,
  input  [31:0] WD,
  output [31:0] RD1,
  output [31:0] RD2
);

  wire [31:0] in1, in2, in3, in4, in5, in6, in7, in8, in9, in10, in11, in12, in13, in14, in15, in16, in17,
       in18, in19, in20, in21, in22, in23, in24, in25, in26, in27, in28, in29, in30, in31, out0, out1, out2,
       out3, out4, out5, out6, out7, out8, out9, out10, out11, out12, out13, out14, out15, out16, out17,
       out18, out19, out20, out21, out22, out23, out24, out25, out26, out27, out28, out29, out30, out31;

  Register #(.width(32)) _8 (.D(in8), .en(RegWrite), .Q(out8), .clk(clk), .clr(reset));
  Register #(.width(32)) _26 (.D(in26), .en(RegWrite), .Q(out26), .clk(clk), .clr(reset));
  Register #(.width(32)) _0 (.D({32{1'b0}}), .en(RegWrite), .Q(out0), .clk(clk), .clr(reset));
  Register #(.width(32)) _17 (.D(in17), .en(RegWrite), .Q(out17), .clk(clk), .clr(reset));
  Multiplexer #(.select(5), .width(32), .enable("false")) multiplexer_1 (
    .in0(out0), .in1(out1), .in2(out2), .in3(out3), .in4(out4), .in5(out5), .in6(out6), .in7(out7),
    .in8(out8), .in9(out9), .in10(out10), .in11(out11), .in12(out12), .in13(out13), .in14(out14),
    .in15(out15), .in16(out16), .in17(out17), .in18(out18), .in19(out19), .in20(out20), .in21(out21),
    .in22(out22), .in23(out23), .in24(out24), .in25(out25), .in26(out26), .in27(out27), .in28(out28),
    .in29(out29), .in30(out30), .in31(out31), .out(RD1), .sel(A1));
  Register #(.width(32)) _1 (.D(in1), .en(RegWrite), .Q(out1), .clk(clk), .clr(reset));
  Register #(.width(32)) _9 (.D(in9), .en(RegWrite), .Q(out9), .clk(clk), .clr(reset));
  Register #(.width(32)) _18 (.D(in18), .en(RegWrite), .Q(out18), .clk(clk), .clr(reset));
  Register #(.width(32)) _27 (.D(in27), .en(RegWrite), .Q(out27), .clk(clk), .clr(reset));
  Register #(.width(32)) _10 (.D(in10), .en(RegWrite), .Q(out10), .clk(clk), .clr(reset));
  Register #(.width(32)) _19 (.D(in19), .en(RegWrite), .Q(out19), .clk(clk), .clr(reset));
  Register #(.width(32)) _28 (.D(in28), .en(RegWrite), .Q(out28), .clk(clk), .clr(reset));
  Multiplexer #(.select(5), .width(32), .enable("false")) multiplexer_2 (
    .in0(out0), .in1(out1), .in2(out2), .in3(out3), .in4(out4), .in5(out5), .in6(out6), .in7(out7),
    .in8(out8), .in9(out9), .in10(out10), .in11(out11), .in12(out12), .in13(out13), .in14(out14),
    .in15(out15), .in16(out16), .in17(out17), .in18(out18), .in19(out19), .in20(out20), .in21(out21),
    .in22(out22), .in23(out23), .in24(out24), .in25(out25), .in26(out26), .in27(out27), .in28(out28),
    .in29(out29), .in30(out30), .in31(out31), .out(RD2), .sel(A2));
  Register #(.width(32)) _2 (.D(in2), .en(RegWrite), .Q(out2), .clk(clk), .clr(reset));
  Register #(.width(32)) _11 (.D(in11), .en(RegWrite), .Q(out11), .clk(clk), .clr(reset));
  Register #(.width(32)) _20 (.D(in20), .en(RegWrite), .Q(out20), .clk(clk), .clr(reset));
  Register #(.width(32)) _29 (.D(in29), .en(RegWrite), .Q(out29), .clk(clk), .clr(reset));
  Demultiplexer #(.select(5), .width(32), .tristate("true"), .enable("false")) demultiplexer_1 (
    .out1(in1), .out2(in2), .out3(in3), .out4(in4), .out5(in5), .out6(in6), .out7(in7), .out8(in8),
    .out9(in9), .out10(in10), .out11(in11), .out12(in12), .out13(in13), .out14(in14), .out15(in15),
    .out16(in16), .out17(in17), .out18(in18), .out19(in19), .out20(in20), .out21(in21), .out22(in22),
    .out23(in23), .out24(in24), .out25(in25), .out26(in26), .out27(in27), .out28(in28), .out29(in29),
    .out30(in30), .out31(in31), .in(WD), .sel(A3));  // open: out0
  Register #(.width(32)) _3 (.D(in3), .en(RegWrite), .Q(out3), .clk(clk), .clr(reset));
  Register #(.width(32)) _12 (.D(in12), .en(RegWrite), .Q(out12), .clk(clk), .clr(reset));
  Register #(.width(32)) _21 (.D(in21), .en(RegWrite), .Q(out21), .clk(clk), .clr(reset));
  Register #(.width(32)) _30 (.D(in30), .en(RegWrite), .Q(out30), .clk(clk), .clr(reset));
  Register #(.width(32)) _4 (.D(in4), .en(RegWrite), .Q(out4), .clk(clk), .clr(reset));
  Register #(.width(32)) _13 (.D(in13), .en(RegWrite), .Q(out13), .clk(clk), .clr(reset));
  Register #(.width(32)) _31 (.D(in31), .en(RegWrite), .Q(out31), .clk(clk), .clr(reset));
  Register #(.width(32)) _5 (.D(in5), .en(RegWrite), .Q(out5), .clk(clk), .clr(reset));
  Register #(.width(32)) _22 (.D(in22), .en(RegWrite), .Q(out22), .clk(clk), .clr(reset));
  Register #(.width(32)) _14 (.D(in14), .en(RegWrite), .Q(out14), .clk(clk), .clr(reset));
  Register #(.width(32)) _23 (.D(in23), .en(RegWrite), .Q(out23), .clk(clk), .clr(reset));
  Register #(.width(32)) _6 (.D(in6), .en(RegWrite), .Q(out6), .clk(clk), .clr(reset));
  Register #(.width(32)) _15 (.D(in15), .en(RegWrite), .Q(out15), .clk(clk), .clr(reset));
  Register #(.width(32)) _24 (.D(in24), .en(RegWrite), .Q(out24), .clk(clk), .clr(reset));
  Register #(.width(32)) _7 (.D(in7), .en(RegWrite), .Q(out7), .clk(clk), .clr(reset));
  Register #(.width(32)) _16 (.D(in16), .en(RegWrite), .Q(out16), .clk(clk), .clr(reset));
  Register #(.width(32)) _25 (.D(in25), .en(RegWrite), .Q(out25), .clk(clk), .clr(reset));

  // Other names for the same wires on the sheet: WE = RegWrite
endmodule

module ALU (
  input  [2:0] op,
  input  [31:0] inA,
  input  [31:0] inB,
  output Zero,
  output [31:0] ALUResult
);

  wire [31:0] adder_1_out, and_1_out, or_1_out, shifter_1_out, subtractor_1_out;

  Adder #(.width(32)) adder_1 (.a(inA), .b(inB), .out(adder_1_out));  // open: cin, cout
  Subtractor #(.width(32)) subtractor_1 (.a(inA), .b(inB), .out(subtractor_1_out));  // open: bin, bout
  Shifter #(.width(32)) shifter_1 (.in(inB), .\dist (5'b10000), .out(shifter_1_out));
  assign and_1_out = inA & inB;  // AND_Gate and_1, 32 bits wide
  assign or_1_out = inA | inB;  // OR_Gate or_1, 32 bits wide
  Multiplexer #(.select(3), .width(32), .enable("false")) multiplexer_1 (
    .in0(adder_1_out), .in1(subtractor_1_out), .in2(and_1_out), .in3(or_1_out), .in4(shifter_1_out),
    .out(ALUResult), .sel(op));  // open: in5, in6, in7
  Comparator #(.width(32), .mode("unsigned")) comparator_1 (.a(inA), .b(inB), .eq(Zero));  // open: gt, lt

  // Other names for the same wires on the sheet: res[31:0] = ALUResult

  // Notes on the sheet:
  //   'd0: +
  //   'd1: - 
  //   'd2: &
  //   'd3: |
  //   'd4: 左移16位
endmodule

module DM (
  input  WE,
  input  [31:0] ALUResult,
  input  [31:0] WD,
  input  clk,
  input  reset,
  output [31:0] RD
);

  RAM #(.addrWidth(5), .dataWidth(32), .bus("separate")) ram_1 (
    .addr(ALUResult[6:2]), .din(WD), .data(RD), .str(WE), .clk(clk), .clr(reset));  // open: sel, ld
endmodule

module EXT (
  input  [15:0] imm,
  input  sign,
  output [31:0] SignImm
);

  wire [31:0] bit_extender_1_out, bit_extender_2_out;

  assign bit_extender_1_out = {{16{1'b0}}, imm};  // Bit_Extender bit_extender_1
  assign bit_extender_2_out = {{16{imm[15]}}, imm};  // Bit_Extender bit_extender_2
  Multiplexer #(.width(32), .disabled(0)) multiplexer_1 (
    .in0(bit_extender_1_out), .in1(bit_extender_2_out), .out(SignImm), .sel(sign));  // open: en
endmodule

module IFU (
  input  clk,
  input  reset,
  input  [31:0] PC_in,
  output [31:0] Instr,
  output [31:0] PC_4,
  output [31:0] PC
);

  Register #(.width(32)) u_PC (.D(PC_in), .Q(PC), .clk(clk), .clr(reset));  // open: en
  Adder #(.width(32)) adder_1 (.a(PC), .b(32'h4), .out(PC_4));  // open: cin, cout
  ROM #(.addrWidth(5), .dataWidth(32)) rom_1 (.addr(PC[6:2]), .data(Instr));  // open: sel

  // Notes on the sheet:
  //   IM
  //   contents of rom_1 (hex, n*v repeats v):
  //   34080064 34090032 340a00fa 340c0096 340b0004 ad680000 8d700000 a9040013 112a0003 1284821 8000c07
endmodule

module Controller (
  input  [5:0] op,
  input  [5:0] func,
  output sign,
  output Branch,
  output MemWrite,
  output RegWrite,
  output MemtoReg,
  output ALUsrc,
  output RegDst,
  output [2:0] ALUControl,
  output PCj,
  output jalsave,
  output jr,
  output lwor
);

  wire addu, addutmp, beq, j, jrtmp, lui, lw, not_1_out, not_2_out, not_3_out, not_4_out, not_5_out,
       not_6_out, not_7_out, not_8_out, not_9_out, not_10_out, not_11_out, not_12_out, ori, subu, subutmp, sw;

  not not_1 (not_1_out, func[5]);
  not not_2 (not_2_out, op[5]);
  not not_3 (not_3_out, func[4]);
  not not_4 (not_4_out, op[4]);
  not not_5 (not_5_out, func[3]);
  not not_6 (not_6_out, op[3]);
  not not_7 (not_7_out, func[2]);
  not not_8 (not_8_out, op[2]);
  not not_9 (not_9_out, func[1]);
  not not_10 (not_10_out, op[1]);
  not not_11 (not_11_out, func[0]);
  not not_12 (not_12_out, op[0]);
  and u_addu (addutmp, func[5], not_3_out, not_5_out, not_7_out, not_9_out, func[0]);
  and u_subu (subutmp, func[5], not_3_out, not_5_out, not_7_out, func[1], func[0]);
  and u_jr (jrtmp, not_1_out, not_3_out, func[3], not_7_out, not_9_out, not_11_out);
  and u_ori (ori, not_2_out, not_4_out, op[3], op[2], not_10_out, op[0]);
  and u_lw (lw, op[5], not_4_out, not_6_out, not_8_out, op[1], op[0]);
  and u_sw (sw, op[5], not_4_out, op[3], not_8_out, op[1], op[0]);
  and u_beq (beq, not_2_out, not_4_out, not_6_out, op[2], not_10_out, not_12_out);
  and u_lui (lui, not_2_out, not_4_out, op[3], op[2], op[1], op[0]);
  and addu_2 (addu, not_2_out, not_4_out, not_6_out, not_8_out, not_10_out, not_12_out, addutmp);
  and subu_2 (subu, not_2_out, not_4_out, not_6_out, not_8_out, not_10_out, not_12_out, subutmp);
  and u_j (j, not_2_out, not_4_out, not_6_out, not_8_out, op[1], not_12_out);
  and jal (jalsave, not_2_out, not_4_out, not_6_out, not_8_out, op[1], op[0]);
  and jr_2 (jr, not_2_out, not_4_out, not_6_out, not_8_out, not_10_out, not_12_out, jrtmp);
  and u_lwor (lwor, op[5], not_4_out, op[3], not_8_out, op[1], not_12_out);
  or u_regdst (RegDst, addu, subu);
  or u_PCj (PCj, jalsave, j);
  or u_ALUsrc (ALUsrc, ori, lw, sw, lui);
  or u_MemtoReg (MemtoReg, lw, lwor);
  or u_RegWrite (RegWrite, jalsave, addu, subu, ori, lw, lui, lwor);
  buf u_MemWrite (MemWrite, sw);  // OR_Gate
  or or_1 (ALUControl[1], ori, 1'b0);
  buf u_Branch (Branch, beq);  // OR_Gate
  or or_2 (ALUControl[2], lui, 1'b0);
  or or_3 (ALUControl[0], subu, ori, beq, 1'b0);
  or u_sign (sign, lwor, lw, sw, beq);

  // Other names for the same wires on the sheet: jal = jalsave
endmodule

module aluctrl (
  input  add,
  input  sub,
  input  ori,
  input  lw,
  input  sw,
  input  beq,
  input  lui,
  output alu2,
  output alu1,
  output alu0
);

  wire and_1_out, and_2_out, not_1_out, not_2_out, not_3_out, not_4_out;

  not not_1 (not_1_out, add);
  not not_2 (not_2_out, lw);
  not not_3 (not_3_out, sw);
  not not_4 (not_4_out, lui);
  and and_1 (and_1_out, not_1_out, not_2_out);
  and and_2 (and_2_out, not_3_out, not_4_out);
  and and_3 (alu0, and_1_out, and_2_out);

  assign alu1 = ori;
  assign alu2 = lui;
endmodule
